// Digital circuit 6bit_FullAdder.dig as structural Verilog
module _6bit_FullAdder (
  input  B4,
  input  A4,
  input  B3,
  input  A3,
  input  A2,
  input  B2,
  input  A1,
  input  B1,
  input  B0,
  input  A0,
  input  B5,
  input  A5,
  output S4,
  output S3,
  output S2,
  output S1,
  output S0,
  output S5,
  output C
);

  wire add_2_c_o, add_3_c_o, add_4_c_o, add_5_c_o, add_6_c_o;

  Add add_1 (.a(B5), .b(A5), .c_i(add_2_c_o), .s(S5), .c_o(C));
  Add add_2 (.a(B4), .b(A4), .c_i(add_3_c_o), .s(S4), .c_o(add_2_c_o));
  Add add_3 (.a(B3), .b(A3), .c_i(add_4_c_o), .s(S3), .c_o(add_3_c_o));
  Add add_4 (.a(B2), .b(A2), .c_i(add_5_c_o), .s(S2), .c_o(add_4_c_o));
  Add add_5 (.a(B1), .b(A1), .c_i(add_6_c_o), .s(S1), .c_o(add_5_c_o));
  Add add_6 (.a(B0), .b(A0), .c_i(1'b0), .s(S0), .c_o(add_6_c_o));
endmodule
