// Digital circuit SequentialMultiplier_SignedNumbers.dig as structural Verilog
module SequentialMultiplier_SignedNumbers (
  input  Clk,
  input  multiplicand3,
  input  multiplicand2,
  input  multiplicand1,
  input  multiplicand0,
  input  mult0,
  input  mult1,
  input  mult2,
  input  mult3,
  input  reset,
  input  multiplicand4,
  input  multiplicand5,
  input  mult4,
  output finish,
  output prod0,
  output prod1,
  output prod2,
  output prod3,
  output prod4,
  output prod5,
  output prod6,
  output prod7,
  output prod8,
  output prod9,
  output sign
);

  wire _6bit_fulladder_1_s0, _6bit_fulladder_1_s1, _6bit_fulladder_1_s2, _6bit_fulladder_1_s3,
       _6bit_fulladder_1_s4, A0_q, A1_q, A2_q, A3_q, A4_q, A5_q, C_Q, carry_bit, FA_MSB, mult0_t,
       multiplexer_1_out, multiplexer_2_out, multiplexer_3_out, multiplexer_4_out, multiplexer_5_out,
       multiplexer_6_out, mux_sel, regQ1, regQ2, regQ3, regQ4, regQ5, regQ6, regQ7, regQ8, regQ9, shift_en;

  D_FF A5 (.D(multiplicand5), .C(Clk), .Q(A5_q));  // open: nQ
  D_FF A4 (.D(multiplicand4), .C(Clk), .Q(A4_q));  // open: nQ
  D_FF A3 (.D(multiplicand3), .C(Clk), .Q(A3_q));  // open: nQ
  D_FF A2 (.D(multiplicand2), .C(Clk), .Q(A2_q));  // open: nQ
  D_FF A1 (.D(multiplicand1), .C(Clk), .Q(A1_q));  // open: nQ
  D_FF A0 (.D(multiplicand0), .C(Clk), .Q(A0_q));  // open: nQ
  Multiplexer multiplexer_1 (.sel(mux_sel), .in_0(1'b0), .in_1(A5_q), .out(multiplexer_1_out));
  D_FF d_ff_1 (.D(carry_bit), .C(Clk), .Q(C_Q));  // open: nQ
  _6bit_FullAdder _6bit_fulladder_1 (
    .B4(regQ9), .A4(multiplexer_2_out), .B3(regQ8), .A3(multiplexer_3_out), .A2(multiplexer_4_out),
    .B2(regQ7), .A1(multiplexer_5_out), .B1(regQ6), .B0(regQ5), .A0(multiplexer_6_out), .B5(C_Q),
    .A5(multiplexer_1_out), .S4(_6bit_fulladder_1_s4), .S3(_6bit_fulladder_1_s3), .S2(_6bit_fulladder_1_s2),
    .S1(_6bit_fulladder_1_s1), .S0(_6bit_fulladder_1_s0), .S5(FA_MSB));  // open: C
  Multiplexer multiplexer_2 (.sel(mux_sel), .in_0(1'b0), .in_1(A4_q), .out(multiplexer_2_out));
  Multiplexer multiplexer_3 (.sel(mux_sel), .in_0(1'b0), .in_1(A3_q), .out(multiplexer_3_out));
  LED led_1 (.in(C_Q));
  Shift_Register_SM2 shift_register_sm2_1 (
    .In4(_6bit_fulladder_1_s4), .Shift(shift_en), .C(C_Q), .In2(_6bit_fulladder_1_s2),
    .In1(_6bit_fulladder_1_s1), .In0(_6bit_fulladder_1_s0), .clk(Clk), .reset(reset),
    .In3(_6bit_fulladder_1_s3), .out_LSB(regQ5), .Out4(regQ9), .Out2(regQ7), .Out1(regQ6), .Out3(regQ8));
  Multiplexer multiplexer_4 (.sel(mux_sel), .in_0(1'b0), .in_1(A2_q), .out(multiplexer_4_out));
  Multiplexer multiplexer_5 (.sel(mux_sel), .in_0(1'b0), .in_1(A1_q), .out(multiplexer_5_out));
  Multiplexer multiplexer_6 (.sel(mux_sel), .in_0(1'b0), .in_1(A0_q), .out(multiplexer_6_out));
  Shift_Register_5bits shift_register_5bits_1 (
    .In4(mult4), .Shift(shift_en), .C(regQ5), .In2(mult2), .In1(mult1), .In0(mult0), .clk(Clk),
    .reset(reset), .In3(mult3), .out0(mult0_t), .out1(regQ1), .out2(regQ2), .out4(regQ4), .out3(regQ3));
  twos_complement twos_complement_1 (
    .in0(mult0_t), .inv(sign), .in1(regQ1), .in2(regQ2), .in3(regQ3), .in4(regQ4), .in5(regQ5), .in6(regQ6),
    .in7(regQ7), .in8(regQ8), .in9(regQ9), .prod0(prod0), .prod1(prod1), .prod2(prod2), .prod3(prod3),
    .prod4(prod4), .prod5(prod5), .prod6(prod6), .prod7(prod7), .prod8(prod8), .prod9(prod9));
  control_sequencer control_sequencer_1 (
    .Mult0(mult0_t), .FA_MSB(FA_MSB), .reset(reset), .clk(Clk), .C_Q(C_Q), .regQ9(regQ9),
    .carry_bit(carry_bit), .mux_sel(mux_sel), .shift_en(shift_en), .finish(finish), .compl_en(sign));

  // Other names for the same wires on the sheet: compl_en = sign; rst = reset
endmodule

/* Test case:
reset Clk mult4 mult3 mult2 mult1 mult0 multiplicand5 multiplicand4 multiplicand3 multiplicand2 multiplicand1 multiplicand0 prod9 prod8 prod7 prod6 prod5 prod4 prod3 prod2 prod1 prod0 finish sign
1 0 0 0 0 0 0 0 0 0 0 0 0 0 0 0 0 0 0 0 0 0 0 0 0
1 C 0 1 0 1 1 1 1 0 0 1 1 0 0 0 0 0 0 1 0 1 1 0 0
0 C 0 1 0 1 1 1 1 0 0 1 1 0 0 0 0 0 0 1 0 1 1 0 0
0 C 0 1 0 1 1 1 1 0 0 1 1 1 0 0 1 1 0 1 0 1 1 0 0
0 C 0 1 0 1 1 1 1 0 0 1 1 1 1 0 0 1 1 0 1 0 1 0 0
0 C 0 1 0 1 1 1 1 0 0 1 1 0 1 1 0 0 1 0 1 0 1 0 0
0 C 0 1 0 1 1 1 1 0 0 1 1 1 0 1 1 0 0 1 0 1 0 0 0
0 C 0 1 0 1 1 1 1 0 0 1 1 1 0 1 1 0 0 1 0 1 0 0 0
0 C 0 1 0 1 1 1 1 0 0 1 1 1 1 0 1 1 0 0 1 0 1 0 0
0 C 0 1 0 1 1 1 1 0 0 1 1 0 1 1 1 0 0 0 1 0 1 0 0
0 C 0 1 0 1 1 1 1 0 0 1 1 1 0 1 1 1 0 0 0 1 0 0 0
0 C 0 1 0 1 1 1 1 0 0 1 1 1 0 1 1 1 0 0 0 1 0 0 0
0 C 0 1 0 1 1 1 1 0 0 1 1 0 0 1 0 0 0 1 1 1 1 1 1
*/
