// Digital circuit Shift_Register_5bits.dig as structural Verilog
module Shift_Register_5bits (
  input  In4,
  input  Shift,
  input  C,
  input  In2,
  input  In1,
  input  In0,
  input  clk,
  input  reset,
  input  In3,
  output out0,
  output out1,
  output out2,
  output out4,
  output out3
);

  wire and_1_out, and_2_out, and_3_out, and_4_out, and_5_out, and_6_out, and_7_out, and_8_out, and_9_out,
       and_10_out, and_11_out, and_12_out, and_13_out, and_14_out, and_15_out, not_1_out, not_2_out,
       or_1_out, or_2_out, or_3_out, or_4_out, or_5_out;

  not not_1 (not_1_out, Shift);
  and and_1 (and_1_out, In4, reset);
  and and_2 (and_2_out, Shift, C);
  not not_2 (not_2_out, reset);
  and and_3 (and_3_out, out4, not_2_out, not_1_out);
  or or_1 (or_1_out, and_1_out, and_3_out, and_2_out);
  D_FF d_ff_1 (.D(or_1_out), .C(clk), .Q(out4));  // open: nQ
  and and_4 (and_4_out, In3, reset);
  and and_5 (and_5_out, Shift, out4);
  and and_6 (and_6_out, not_2_out, out3, not_1_out);
  or or_2 (or_2_out, and_4_out, and_6_out, and_5_out);
  D_FF d_ff_2 (.D(or_2_out), .C(clk), .Q(out3));  // open: nQ
  and and_7 (and_7_out, In2, reset);
  and and_8 (and_8_out, Shift, out3);
  and and_9 (and_9_out, not_2_out, out2, not_1_out);
  or or_3 (or_3_out, and_7_out, and_9_out, and_8_out);
  D_FF d_ff_3 (.D(or_3_out), .C(clk), .Q(out2));  // open: nQ
  and and_10 (and_10_out, In1, reset);
  and and_11 (and_11_out, Shift, out2);
  and and_12 (and_12_out, not_2_out, out1, not_1_out);
  or or_4 (or_4_out, and_10_out, and_12_out, and_11_out);
  D_FF d_ff_4 (.D(or_4_out), .C(clk), .Q(out1));  // open: nQ
  and and_13 (and_13_out, In0, reset);
  and and_14 (and_14_out, Shift, out1);
  and and_15 (and_15_out, not_2_out, out0, not_1_out);
  or or_5 (or_5_out, and_13_out, and_15_out, and_14_out);
  D_FF d_ff_5 (.D(or_5_out), .C(clk), .Q(out0));  // open: nQ
endmodule
