// Digital circuit Shift_Register_SM2.dig as structural Verilog
module Shift_Register_SM2 (
  input  In4,
  input  Shift,
  input  C,
  input  In2,
  input  In1,
  input  In0,
  input  clk,
  input  reset,
  input  In3,
  output out_LSB,
  output Out4,
  output Out2,
  output Out1,
  output Out3
);

  wire and_1_out, and_2_out, and_3_out, and_4_out, and_5_out, and_6_out, and_7_out, and_8_out, and_9_out,
       and_10_out, and_11_out, and_12_out, and_13_out, and_14_out, and_15_out, not_1_out, not_2_out,
       or_1_out, or_2_out, or_3_out, or_4_out, or_5_out;

  not not_1 (not_1_out, Shift);
  and and_1 (and_1_out, In4, not_1_out);
  and and_2 (and_2_out, Shift, C);
  not not_2 (not_2_out, reset);
  or or_1 (or_1_out, and_1_out, and_2_out);
  and and_3 (and_3_out, not_2_out, or_1_out);
  D_FF d_ff_1 (.D(and_3_out), .C(clk), .Q(Out4));  // open: nQ
  and and_4 (and_4_out, In3, not_1_out);
  and and_5 (and_5_out, Shift, Out4);
  or or_2 (or_2_out, and_4_out, and_5_out);
  and and_6 (and_6_out, not_2_out, or_2_out);
  D_FF d_ff_2 (.D(and_6_out), .C(clk), .Q(Out3));  // open: nQ
  and and_7 (and_7_out, In2, not_1_out);
  and and_8 (and_8_out, Shift, Out3);
  or or_3 (or_3_out, and_7_out, and_8_out);
  and and_9 (and_9_out, not_2_out, or_3_out);
  D_FF d_ff_3 (.D(and_9_out), .C(clk), .Q(Out2));  // open: nQ
  and and_10 (and_10_out, In1, not_1_out);
  and and_11 (and_11_out, Shift, Out2);
  or or_4 (or_4_out, and_10_out, and_11_out);
  and and_12 (and_12_out, not_2_out, or_4_out);
  D_FF d_ff_4 (.D(and_12_out), .C(clk), .Q(Out1));  // open: nQ
  and and_13 (and_13_out, In0, not_1_out);
  and and_14 (and_14_out, Shift, Out1);
  or or_5 (or_5_out, and_13_out, and_14_out);
  and and_15 (and_15_out, not_2_out, or_5_out);
  D_FF d_ff_5 (.D(and_15_out), .C(clk), .Q(out_LSB));  // open: nQ
endmodule
