// Digital circuit control_sequencer.dig as structural Verilog
module control_sequencer (
  input  Mult0,
  input  FA_MSB,
  input  reset,
  input  clk,
  input  C_Q,
  input  regQ9,
  output carry_bit,
  output mux_sel,
  output shift_en,
  output finish,
  output compl_en
);

  wire and_1_out, and_2_out, and_7_out, and_8_out, and_9_out, and_10_out, count_out, D0, D1, Q0, Q0_bar, Q1,
       Q1_bar, reset_bar;

  not not_1 (reset_bar, reset);
  and and_1 (and_1_out, reset_bar, Q0, FA_MSB);
  and and_2 (and_2_out, reset_bar, Q1, C_Q);
  and and_3 (mux_sel, reset_bar, Q0, Q1_bar, Mult0);
  and and_4 (shift_en, reset_bar, Q1, Q0_bar);
  and and_5 (finish, reset_bar, Q1, Q0);
  and and_6 (compl_en, reset_bar, Q0, Q1, regQ9);
  or or_1 (carry_bit, and_1_out, and_2_out);
  D_FF d_ff_1 (.D(D0), .C(clk), .Q(Q0), .nQ(Q0_bar));
  D_FF d_ff_2 (.D(D1), .C(clk), .Q(Q1), .nQ(Q1_bar));
  and and_7 (and_7_out, reset_bar, Q1);
  and and_8 (and_8_out, reset_bar, Q0_bar);
  and and_9 (and_9_out, reset_bar, count_out, Q1);
  and and_10 (and_10_out, reset_bar, Q0);
  counter_SM5 counter_sm5_1 (.reset(reset), .clk(clk), .state2(Q1), .out(count_out));
  or or_2 (D0, and_7_out, and_8_out);
  or or_3 (D1, and_9_out, and_10_out);

  // Notes on the sheet:
  //   Name:
  //   st0bb3n
  //   Section:
endmodule
