// Digital circuit counter_SM5.dig as structural Verilog
module counter_SM5 (
  input  reset,
  input  clk,
  input  state2,
  output out
);

  wire and_1_out, and_2_out, and_3_out, d_ff_1_nq, d_ff_1_q, d_ff_2_nq, d_ff_2_q, d_ff_3_nq, d_ff_3_q,
       multiplexer_1_out, multiplexer_2_out, multiplexer_3_out, not_1_out, not_2_out;

  not not_1 (not_1_out, reset);
  and and_1 (and_1_out, not_1_out, d_ff_1_nq);
  Multiplexer multiplexer_1 (.sel(reset), .in_0(state2), .in_1(clk), .out(multiplexer_1_out));
  D_FF d_ff_1 (.D(and_1_out), .C(multiplexer_1_out), .Q(d_ff_1_q), .nQ(d_ff_1_nq));
  and and_2 (and_2_out, not_1_out, d_ff_2_nq);
  Multiplexer multiplexer_2 (.sel(reset), .in_0(d_ff_1_nq), .in_1(clk), .out(multiplexer_2_out));
  D_FF d_ff_2 (.D(and_2_out), .C(multiplexer_2_out), .Q(d_ff_2_q), .nQ(d_ff_2_nq));
  and and_3 (and_3_out, not_1_out, d_ff_3_nq);
  Multiplexer multiplexer_3 (.sel(reset), .in_0(d_ff_2_nq), .in_1(clk), .out(multiplexer_3_out));
  D_FF d_ff_3 (.D(and_3_out), .C(multiplexer_3_out), .Q(d_ff_3_q), .nQ(d_ff_3_nq));
  not not_2 (not_2_out, d_ff_2_q);
  and and_4 (out, d_ff_3_q, not_2_out, d_ff_1_q);
endmodule
