// Digital circuit twos_complement.dig as structural Verilog
module twos_complement (
  input  in0,
  input  inv,
  input  in1,
  input  in2,
  input  in3,
  input  in4,
  input  in5,
  input  in6,
  input  in7,
  input  in8,
  input  in9,
  output prod0,
  output prod1,
  output prod2,
  output prod3,
  output prod4,
  output prod5,
  output prod6,
  output prod7,
  output prod8,
  output prod9
);

  wire FA_4_7_pin13, FA_8_9_pin13, xor_1_out, xor_2_out, xor_3_out, xor_4_out, xor_5_out, xor_6_out,
       xor_7_out, xor_8_out, xor_9_out, xor_10_out;

  xor xor_1 (xor_1_out, in9, inv);
  xor xor_2 (xor_2_out, in8, inv);
  xor xor_3 (xor_3_out, in7, inv);
  xor xor_4 (xor_4_out, in6, inv);
  xor xor_5 (xor_5_out, in5, inv);
  xor xor_6 (xor_6_out, in4, inv);
  xor xor_7 (xor_7_out, in3, inv);
  xor xor_8 (xor_8_out, in2, inv);
  xor xor_9 (xor_9_out, in1, inv);
  xor xor_10 (xor_10_out, in0, inv);
  _7483 FA_8_9 (
    .pin1(1'b0), .pin3(1'b0), .pin4(1'b0), .pin5(1'b1), .pin6(prod9), .pin7(1'b0), .pin8(xor_1_out),
    .pin9(prod8), .pin10(xor_2_out), .pin11(1'b0), .pin12(1'b0), .pin13(FA_8_9_pin13), .pin16(1'b0));  // open: pin2, pin14, pin15
  _7483 FA_4_7 (
    .pin1(xor_3_out), .pin2(prod6), .pin3(xor_4_out), .pin4(1'b0), .pin5(1'b1), .pin6(prod5), .pin7(1'b0),
    .pin8(xor_5_out), .pin9(prod4), .pin10(xor_6_out), .pin11(1'b0), .pin12(1'b0), .pin13(FA_4_7_pin13),
    .pin14(FA_8_9_pin13), .pin15(prod7), .pin16(1'b0));
  _7483 FA_0_3 (
    .pin1(xor_7_out), .pin2(prod2), .pin3(xor_8_out), .pin4(1'b0), .pin5(1'b1), .pin6(prod1), .pin7(1'b0),
    .pin8(xor_9_out), .pin9(prod0), .pin10(xor_10_out), .pin11(inv), .pin12(1'b0), .pin13(1'b0),
    .pin14(FA_4_7_pin13), .pin15(prod3), .pin16(1'b0));
endmodule
